# Fritzing sketch Radiodan_app (saved by Fritzing 0.8.3b)

parts:
  SW1 = ENCODER_RGB_CA [package=encoder_led_3]
  R1 = Resistor [tolerance=±5% resistance=220 package=THT]
  R3 = Resistor [tolerance=±5% resistance=220 package=THT]
  R2 = Resistor [tolerance=±5% resistance=220 package=THT]
  SW2 = ENCODER_RGB_CA [package=encoder_led_3]
  R4 = Resistor [tolerance=±5% resistance=220 package=THT]
  R6 = Resistor [tolerance=±5% resistance=220 package=THT]
  R5 = Resistor [tolerance=±20% resistance=220 package=THT]
  Momentary_Button = Pushbutton [package=THT]
  RaspberryPi1 = Raspberry Pi Model B

nets:
  N1: SW1.-R, RaspberryPi1.SDA
  N2: SW1.SW, RaspberryPi1.SCL
  N3: SW1.+, R3.Pin_0
  N4: SW1.A, RaspberryPi1.#4
  N5: SW1.B, R2.Pin_0
  N6: SW1.C, R1.Pin_0
  N7: R1.Pin_1, RaspberryPi1.MOSI
  N8: R3.Pin_1, RaspberryPi1.SCLK
  N9: R2.Pin_1, RaspberryPi1.MISO
  N10: SW2.-R, RaspberryPi1.#24
  N11: SW2.SW, RaspberryPi1.#23
  N12: SW2.-B, RaspberryPi1.5V
  N13: SW2.+, R5.Pin_1
  N14: SW2.A, RaspberryPi1.#22
  N15: SW2.B, R4.Pin_1
  N16: SW2.C, R6.Pin_1
  N17: R4.Pin_0, RaspberryPi1.CS0
  N18: R6.Pin_0, RaspberryPi1.#25
  N19: R5.Pin_0, RaspberryPi1.CS1
  N20: Momentary_Button.leg0, RaspberryPi1.GND
  N21: Momentary_Button.leg1, RaspberryPi1.#21

custom parts:
  Raspberry Pi Model B: Raspberry Pi (Model B)
