# Fritzing sketch Radiodan_app_simple (saved by Fritzing 0.8.3b)

parts:
  S2 = SWITCH-MOMENTARY-2 [package=tactile-pth]
  S1 = SWITCH-MOMENTARY-2 [package=tactile-pth]
  LED1 = RGB LED (com. cathode, rbg) [package="5 mm [THT]"]
  RaspberryPi1 = Raspberry Pi Model B
  R1 = Resistor [tolerance=±20% resistance=10k package=THT]  # not connected

nets:
  N1: S2.1, RaspberryPi1.#4
  N2: S1.1, RaspberryPi1.#21
  N3: LED1.red_anode, RaspberryPi1.MOSI
  N4: LED1.blue_anode, RaspberryPi1.SCLK
  N5: LED1.green_anode, RaspberryPi1.MISO

custom parts:
  Raspberry Pi Model B: Raspberry Pi (Model B)
